# Fritzing sketch scheme (saved by Fritzing 0.9.10b)

parts:
  SERVO17 = Tower Pro SG90 servo [part_number=101246]  # not connected
  SERVO8 = Tower Pro SG90 servo [part_number=101246]  # not connected
  SERVO24 = Tower Pro SG90 servo [part_number=101246]  # not connected
  SERVO2 = Tower Pro SG90 servo [part_number=101246]  # not connected
  Power_plug1 = Power plug
  SERVO21 = Tower Pro SG90 servo [part_number=101246]  # not connected
  SERVO19 = Tower Pro SG90 servo [part_number=101246]  # not connected
  SERVO20 = Tower Pro SG90 servo [part_number=101246]  # not connected
  SERVO6 = Tower Pro SG90 servo [part_number=101246]  # not connected
  SERVO15 = Tower Pro SG90 servo [part_number=101246]  # not connected
  SERVO7 = Tower Pro SG90 servo [part_number=101246]  # not connected
  Компонент2 = 16-Channel 12-bit PWM Servo Driver - I2C [part_number=815]
  Компонент1 = Arduino Uno (Rev3) - ICSP
  Компонент3 = 16-Channel 12-bit PWM Servo Driver - I2C [part_number=815]
  SERVO5 = Tower Pro SG90 servo [part_number=101246]  # not connected
  SERVO22 = Tower Pro SG90 servo [part_number=101246]  # not connected
  SERVO1 = Tower Pro SG90 servo [part_number=101246]  # not connected
  SERVO16 = Tower Pro SG90 servo [part_number=101246]  # not connected
  SERVO3 = Tower Pro SG90 servo [part_number=101246]  # not connected
  SERVO4 = Tower Pro SG90 servo [part_number=101246]  # not connected
  SERVO18 = Tower Pro SG90 servo [part_number=101246]  # not connected

nets:
  GND: Power_plug1.GND, Компонент2.GND, Компонент1.GND, Компонент3.GND
  N1: Power_plug1.VCC, Компонент3.PWRIN
  N2: Компонент2.5.0V, Компонент3.5.0V
  VCC: Компонент2.VCC, Компонент1.5V, Компонент3.VCC
  N3: Компонент2.SDA, Компонент1.A4/SDA, Компонент3.SDA
  N4: Компонент2.SCL, Компонент1.A5/SCL, Компонент3.SCL
  N5: Компонент2.OE, Компонент3.OE

custom parts:
  Tower Pro SG90 servo: Original file by John De Cristofaro http://www.adafruit.com/products/1449 Adafruit Feedback Servo (Small) Edited by: e-radionica.com 28/9/2015
  16-Channel 12-bit PWM Servo Driver - I2C: You want to make a cool robot, maybe a hexapod walker, or maybe just a piece of art with a lot of moving parts. Or maybe you want to drive a lot of LEDs with precise PWM output. Using only two pins, control 16 free-running PWM outputs! You can even chain up 62 breakouts to control up to 992 PWM outputs.
